# Fritzing sketch dooor sensor (saved by Fritzing 0.8.7b)
breadboards: 1

parts:
  Raspberry_Pi_B_rev1 = Raspberry Pi B rev2
  PIR1 = PIR sensor
  J5 = Piezo Speaker
  R1 = Resistor [tolerance=±5% resistance=220 package=THT]

nets:
  GND: Raspberry_Pi_B_rev1.GND, PIR1.GND, J5.pin1
  N1: Raspberry_Pi_B_rev1.GPIO_4, J5.pin2
  5V: Raspberry_Pi_B_rev1.5V, PIR1.VDD
  N2: PIR1.SIG, R1.Pin_1
